# Fritzing sketch LED (saved by Fritzing 0.9.9b)
breadboards: 1

parts:
  A1 = Raspberry Pi Pico W
  LED1 = LED - 5mm [color="Red (633nm)" current=0.030 package="5 mm [THT]"]
  LED2 = smd LED [color="Red (633nm)" current=0.030 package="0603 [SMD]"]
  LED2_2 = smd LED [color="Yellow (595nm)" current=0.030 package="0805 [SMD]"]
  LED3 = LED - 5mm [color="Green (555nm)" current=0.030 package="5 mm [THT]"]
  R1 = Resistor [tolerance=±5% power=0.25 resistance=220 package=THT]

nets:
  N1: A1.pin_3, A1.pin_8, A1.pin_13, A1.pin_18, A1.pin_23, A1.pin_28, A1.pin_33, A1.pin_38, A1.pin_42, LED1.cathode, LED2.cathode, LED2_2.cathode, LED3.cathode, R1.Pin_0
  N2: A1.pin_21, LED3.anode
  N3: A1.pin_24, LED2.anode, LED2_2.anode
  N4: A1.pin_26, R1.Pin_1

notes:
  resister สามารถต่อ ขั้วบวกหรือขั้วลบก็ได้ และ สามารถหันไปในทิศทางใดก

custom parts:
  Raspberry Pi Pico W: Raspberry Pi Pico W. Based around the RP2040 microcontroller the Pico W is a low cost microcontroller device bringing Raspberry Pi quality, cost, and easy of use to the microcontroller space. The areas marked KEEPOUT in pcb silkscreen should not have traces running through them to avoid shorts on a soldered in module!
