# Fritzing sketch OLED_PICO (saved by Fritzing 0.9.9b)

parts:
  Mod1 = Raspberry Pi Pico
  Grove1 = Grove OLED 128x96

nets:
  N1: Mod1.pin_21, Grove1.SDA
  N2: Mod1.pin_22, Grove1.SCL
  N3: Mod1.pin_33, Mod1.pin_38, Grove1.GND
  N4: Mod1.pin_36, Grove1.VCC

custom parts:
  Raspberry Pi Pico: Raspberry Pi Pico. Based around the RP2040 microcontroller the Pico is a low cost microcontroller device bringing Raspberry Pi quality, cost, and easy of use to the microcontroller space. Jan 2021, Split part in to two versions: tht (this one) and SMD. This one will drill holes for a .1 in header in pcb to allow plugging in the module as well as providing pads to solder the module to the top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
